// Digital circuit decoder.dig as structural Verilog
module decoder (
  input  [31:0] i,
  output [15:0] A,
  output [1:0] rs,
  output [1:0] rd
);


  assign A = i[15:0];
  assign rd = i[17:16];
  assign rs = i[21:20];

  // Notes on the sheet:
  //   i: Take 32-bits input
endmodule
