// Digital circuit front.dig as structural Verilog
module front (
  input  [15:0] value,
  input  [1:0] dest,
  input  [1:0] src,
  output [15:0] R0,
  output [15:0] R1,
  output [15:0] R2,
  output [15:0] R3,
  output [15:0] B,
  output [1:0] rs,
  output [15:0] A,
  output [15:0] B_2,
  output [1:0] rd,
  output [3:0] pc,
  output [15:0] A_2
);

  wire add, add_out, advance_out, asm_1_store_clk, jmp_out, jump, mode_out;
  wire [15:0] decoder_1_p9;
  wire [31:0] asm_1_inst, Program_d;

  LED programming (.in(mode_out));
  DipSwitch mode (.out(mode_out));
  Button u_add (.out(add_out));
  Button jmp (.out(jmp_out));
  asm asm_1 (
    .mode(mode_out), .imm(value), .dest(dest), .src(src), .add(add_out), .jump(jmp_out), .inst(asm_1_inst),
    .store_clk(asm_1_store_clk));
  Button advance (.out(advance_out));
  EEPROMDualPort #(.AddrBits(4), .Bits(32)) Program (
    .A(pc), .Din(asm_1_inst), .str(1'b1), .C(asm_1_store_clk), .ld(1'b1), .D(Program_d));
  CounterPreset #(.Bits(4)) u_PC (
    .en(1'b1), .C(advance_out), .dir(1'b0), .in(A[3:0]), .ld(jump), .clr(1'b0), .out(pc));  // open: ovf
  LED add_2 (.in(add));
  LED u_jump (.in(jump));
  // decoder decoder_1: pin names not known; wires that end beside it: mode_out, Program_d, asm_1_inst, A, rs, rd, jump, add, decoder_1_p9
  execute execute_1 (.L(A), .R(B), .add(add));  // open: sum
  regfile regfile_1 (.rs(rs), .rd(rd), .D(decoder_1_p9), .CL(advance_out), .R0(B), .R1(R0), .R2(R1), .R3(R2), .B(R3));

  assign A_2 = A;
  assign B_2 = B;

  // Notes on the sheet:
  //   contents of Program (hex, n*v repeats v):
  //   64,100c8,120063,230022,30002a,7000001
endmodule
